# Fritzing sketch forest_fire_detection_layout (saved by Fritzing 0.9.3b)

parts:
  Part2 = Adafruit AMG8833 [part_number="Adafruit #3538"]
  Raspberry_Pi_1 = Raspberry Pi 3 [part_number=RPI-3-V1.2]
  M1 = NEO-7M GPS Module [part_number=GY-GPSV3-NEO]
  Part3 = MQ-7 breakout
  LED1 = LEDs [package=led10mm]

nets:
  VCC: Part2.VCC, Part2.3.3V, Raspberry_Pi_1.3v3
  GND: Part2.GND, Raspberry_Pi_1.GND, M1.GND, Part3.GND, LED1.C
  N1: Part2.SCL, Raspberry_Pi_1.GPIO3
  N2: Part2.SDA, Raspberry_Pi_1.GPIO2
  N3: Raspberry_Pi_1.GPIO22, Part3.DO
  N4: Raspberry_Pi_1.GPIO23, LED1.A
  N5: Raspberry_Pi_1.GPIO15, M1.Tx
  VCC_2: Raspberry_Pi_1.5V, M1.Vcc, Part3.VCC

custom parts:
  Adafruit AMG8833: Add heat-vision to your project and with an Adafruit AMG8833 Grid-EYE Breakout! This sensor from Panasonic is an 8x8 array of IR thermal sensors. When connected to your microcontroller (or raspberry Pi) it will return an array of 64 individual infrared temperature readings over I2C. It's like those fancy thermal cameras, but compact and simple enough for easy integration. This part will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
  NEO-7M GPS Module: GY-GPSV3-NEO NEO-7M GPS Module Module based on U-blox NEO-7M GPS engine, incorporating regulator for 3.3-5V DC input, MS621FE-compatible rechargeable battery for backup and EEPROM for storing configuration settings. Links: NEO-7 series product information page NEO-7 Datasheet
  MQ-7 breakout: SKU: 101282
